# Fritzing sketch Maina_Sketch_001 (saved by Fritzing 0.9.3b)
breadboards: 1

parts:
  Componente1 = Arduino Nano (Rev3.0)
  Pololu_A1 = Pololu A4988 [package=SO16]
  M1 = Stepper Motor - Bipolar
  J1 = Camdenboss CTB0158-2 [part_number=CTB0158-2 package=THT]
  J2 = Camdenboss CTB0158-2 [part_number=CTB0158-2 package=THT]
  C1 = Capacitor Polarized [package=panasonic_d]
  D2F1 = D2F-FL Omron Snap Action Limit Switch with Level
  D2F2 = D2F-FL Omron Snap Action Limit Switch with Level
  U1 = Optocoupler [package=THT]
  U2 = Optocoupler [package=THT]
  U3 = 3.5mm Audio Jack [package=audio-jack]
  R1 = Resistor [tolerance=±5% resistance=220 package=THT]
  R2 = Resistor [tolerance=±5% resistance=220 package=THT]
  R3 = Resistor [tolerance=±5% resistance=220 package=THT]
  R4 = Resistor [tolerance=±5% resistance=220 package=THT]
  LED2 = LED - 3mm [color="Blue (505nm)" package="3 mm [THT]"]
  LED3 = LED - 3mm [color="Red (660nm)" package="3 mm [THT]"]

nets:
  N1: Componente1.GND, Pololu_A1.GND#8, J1.pin2, D2F2.NC, U1.Pin_2, U1.Pin_4, U2.Pin_2, U2.Pin_4, U3.SLEEVE, LED2.cathode, LED3.cathode
  N2: Componente1.D3, R1.Pin_1, R3.Pin_0
  N3: Componente1.D4, R2.Pin_1, R4.Pin_0
  N4: Componente1.D8, J1.pin1, D2F1.COM
  N5: Componente1.A5, Pololu_A1.STEP
  N6: Componente1.A4, Pololu_A1.DIR
  N7: Componente1.A3, Pololu_A1.ENABLE
  N8: Componente1.A2, Pololu_A1.MS3
  N9: Componente1.A1, Pololu_A1.MS2
  N10: Componente1.A0, Pololu_A1.MS1
  3V3: Componente1.3V3, Pololu_A1.VDD
  N11: Pololu_A1.1B, M1.D
  N12: Pololu_A1.1A, M1.B
  N13: Pololu_A1.2A, M1.C
  N14: Pololu_A1.2B, M1.A
  N15: Pololu_A1.GND#14, J2.pin2, C1.-
  N16: Pololu_A1.VMOT, J2.pin1, C1.+
  N17: D2F1.NC, D2F2.COM
  N18: U1.Pin_1, R1.Pin_0
  N19: U1.Pin_5, U3.RIGHT
  N20: U2.Pin_1, R2.Pin_0
  N21: U2.Pin_5, U3.LEFT
  N22: R3.Pin_1, LED3.anode
  N23: R4.Pin_1, LED2.anode

notes:
  Alimentazione stepper
  Connettore micro finecorsa

custom parts:
  D2F-FL Omron Snap Action Limit Switch with Level: Snap action switch with stainless steel lever.
